// Logisim project SUBLEQ_computer.circ as structural Verilog: 14 circuits, main circuit DesignIdea
module DesignIdea (
  input  in_1
);

  wire and_1_out, and_2_out, and_3_out, and_4_out, clock_1_out, decoder_1_out0, decoder_1_out1,
       decoder_1_out2, decoder_1_out3, decoder_1_out4, decoder_1_out5, decoder_1_out6, decoder_1_out7,
       nor_1_out, not_1_out, not_3_out, or_1_out, or_2_out, or_3_out, or_4_out, or_5_out, or_6_out;
  wire [2:0] counter_2_q;
  wire [15:0] adder_1_out, controlled_buffer_1_out, controlled_buffer_2_out, counter_1_q, not_2_out,
       register_1_q, register_2_q, register_3_q;

  Clock clock_1 (.out(clock_1_out));
  not not_1 (not_1_out, clock_1_out);
  Register #(.width(16)) register_1 (
    .D(controlled_buffer_1_out), .en(or_2_out), .Q(register_1_q), .clk(clock_1_out), .clr(in_1));
  Counter #(.width(16), .max('hffff)) counter_1 (
    .load(and_3_out), .D(controlled_buffer_2_out), .count(or_3_out), .Q(counter_1_q), .clk(clock_1_out),
    .clr(in_1));  // open: carry
  Register #(.width(16)) register_2 (
    .D(controlled_buffer_1_out), .en(decoder_1_out1), .Q(register_2_q), .clk(clock_1_out), .clr(in_1));
  assign not_2_out = ~register_3_q;  // NOT_Gate not_2, 16 bits wide
  Register #(.width(16)) register_3 (
    .D(controlled_buffer_1_out), .en(decoder_1_out3), .Q(register_3_q), .clk(clock_1_out), .clr(in_1));
  assign controlled_buffer_1_out = decoder_1_out4 ? adder_1_out : 16'bz;  // Controlled_Buffer controlled_buffer_1
  assign controlled_buffer_2_out = or_1_out ? register_1_q : 16'bz;  // Controlled_Buffer controlled_buffer_2
  assign controlled_buffer_2_out = or_2_out ? counter_1_q : 16'bz;  // Controlled_Buffer controlled_buffer_3
  and and_1 (and_1_out, not_3_out, or_4_out);
  not not_3 (not_3_out, controlled_buffer_2_out[15]);
  Adder #(.width(16)) adder_1 (.a(register_2_q), .b(not_2_out), .out(adder_1_out), .cin(1'b1));  // open: cout
  or or_1 (or_1_out, decoder_1_out1, decoder_1_out3, decoder_1_out4, and_3_out);
  or or_2 (or_2_out, decoder_1_out0, decoder_1_out2, decoder_1_out5);
  and and_2 (and_2_out, clock_1_out, decoder_1_out4);
  nor nor_1 (nor_1_out, adder_1_out[0], adder_1_out[1], adder_1_out[2], adder_1_out[3], adder_1_out[4], adder_1_out[5], adder_1_out[6], adder_1_out[7], adder_1_out[9], adder_1_out[10], adder_1_out[11], adder_1_out[12], adder_1_out[13], adder_1_out[14], adder_1_out[15], adder_1_out[8]);
  ROM #(.addrWidth(16), .dataWidth(16)) rom_1 (
    .addr(controlled_buffer_2_out), .data(controlled_buffer_1_out), .sel(and_1_out));
  RAM #(.addrWidth(16), .dataWidth(16)) ram_1 (
    .addr(controlled_buffer_2_out), .data(controlled_buffer_1_out), .sel(controlled_buffer_2_out[15]),
    .clk(and_2_out), .ld(or_4_out), .clr(in_1));
  or or_3 (or_3_out, decoder_1_out1, decoder_1_out3, and_4_out);
  or or_4 (or_4_out, decoder_1_out0, decoder_1_out1, decoder_1_out2, decoder_1_out3, decoder_1_out5);
  and and_3 (and_3_out, or_6_out, decoder_1_out6);
  Counter #(.width(3), .max('h7)) counter_2 (
    .load(1'b0), .count(1'b1), .Q(counter_2_q), .clk(not_1_out), .clr(or_5_out));  // open: D, carry
  or or_5 (or_5_out, in_1, decoder_1_out7);
  or or_6 (or_6_out, nor_1_out, adder_1_out[15]);
  and and_4 (and_4_out, ~or_6_out, decoder_1_out6);  // AND_Gate
  Decoder #(.select(3)) decoder_1 (
    .out0(decoder_1_out0), .out1(decoder_1_out1), .out2(decoder_1_out2), .out3(decoder_1_out3),
    .out4(decoder_1_out4), .out5(decoder_1_out5), .out6(decoder_1_out6), .out7(decoder_1_out7),
    .sel(counter_2_q), .en(1'b1));
endmodule

module _74374_OctalReg (
  input  OUTPUT_CONTROL,
  input  D1,
  input  D8,
  input  D2,
  input  D7,
  input  D3,
  input  D6,
  input  D4,
  input  D5,
  input  CLOCK,
  output VCC,
  output Q1,
  output Q8,
  output Q2,
  output Q7,
  output Q3,
  output Q6,
  output Q4,
  output Q5,
  output GND
);

  wire d_ff_1_q, d_ff_2_q, d_ff_3_q, d_ff_4_q, d_ff_5_q, d_ff_6_q, d_ff_7_q, d_ff_8_q;

  assign Q1 = OUTPUT_CONTROL ? d_ff_1_q : 1'bz;  // Controlled_Buffer controlled_buffer_1
  assign Q2 = OUTPUT_CONTROL ? d_ff_2_q : 1'bz;  // Controlled_Buffer controlled_buffer_2
  assign Q3 = OUTPUT_CONTROL ? d_ff_3_q : 1'bz;  // Controlled_Buffer controlled_buffer_3
  assign Q4 = OUTPUT_CONTROL ? d_ff_4_q : 1'bz;  // Controlled_Buffer controlled_buffer_4
  D_Flip_Flop d_ff_1 (.clk(CLOCK), .D(D1), .Q(d_ff_1_q), .preset(1'b0), .en(1'b1), .reset(1'b0));  // open: Qn
  D_Flip_Flop d_ff_2 (.clk(CLOCK), .D(D2), .Q(d_ff_2_q), .preset(1'b0), .en(1'b1), .reset(1'b0));  // open: Qn
  D_Flip_Flop d_ff_3 (.clk(CLOCK), .D(D3), .Q(d_ff_3_q), .preset(1'b0), .en(1'b1), .reset(1'b0));  // open: Qn
  D_Flip_Flop d_ff_4 (.clk(CLOCK), .D(D4), .Q(d_ff_4_q), .preset(1'b0), .en(1'b1), .reset(1'b0));  // open: Qn
  D_Flip_Flop d_ff_5 (.clk(CLOCK), .D(D8), .Q(d_ff_5_q), .preset(1'b0), .en(1'b1), .reset(1'b0));  // open: Qn
  D_Flip_Flop d_ff_6 (.clk(CLOCK), .D(D7), .Q(d_ff_6_q), .preset(1'b0), .en(1'b1), .reset(1'b0));  // open: Qn
  D_Flip_Flop d_ff_7 (.clk(CLOCK), .D(D6), .Q(d_ff_7_q), .preset(1'b0), .en(1'b1), .reset(1'b0));  // open: Qn
  D_Flip_Flop d_ff_8 (.clk(CLOCK), .D(D5), .Q(d_ff_8_q), .preset(1'b0), .en(1'b1), .reset(1'b0));  // open: Qn
  assign Q8 = OUTPUT_CONTROL ? d_ff_5_q : 1'bz;  // Controlled_Buffer controlled_buffer_5
  assign Q7 = OUTPUT_CONTROL ? d_ff_6_q : 1'bz;  // Controlled_Buffer controlled_buffer_6
  assign Q6 = OUTPUT_CONTROL ? d_ff_7_q : 1'bz;  // Controlled_Buffer controlled_buffer_7
  assign Q5 = OUTPUT_CONTROL ? d_ff_8_q : 1'bz;  // Controlled_Buffer controlled_buffer_8

  assign GND = 1'b0;
  assign VCC = 1'b1;
endmodule

module _74283_4bitAdder (
  input  B2,
  input  B3,
  input  A2,
  input  A3,
  input  A1,
  input  A4,
  input  B1,
  input  B4,
  input  C0,
  output Sum2,
  output Vcc,
  output Sum1,
  output Sum3,
  output Sum4,
  output GND,
  output C4
);

  Adder #(.width(4)) adder_1 (
    .a({A4, A3, A2, A1}), .b({B4, B3, B2, B1}), .out({Sum4, Sum3, Sum2, Sum1}), .cin(C0), .cout(C4));

  assign GND = 1'b0;
  assign Vcc = 1'b1;
endmodule

module _74244_OctalTriStateBuffer (
  input  _1OE,
  input  _1A0,
  input  _2OE,
  input  _1A1,
  input  _2A0,
  input  _1A2,
  input  _2A1,
  input  _1A3,
  input  _2A2,
  input  _2A3,
  output VCC,
  output _2Y0,
  output _1Y0,
  output _2Y1,
  output _1Y1,
  output _2Y2,
  output _1Y2,
  output _2Y3,
  output _1Y3,
  output GND
);

  wire not_1_out, not_2_out;

  not not_1 (not_1_out, _1OE);
  assign _1Y0 = not_1_out ? _1A0 : 1'bz;  // Controlled_Buffer controlled_buffer_1
  assign _1Y1 = not_1_out ? _1A1 : 1'bz;  // Controlled_Buffer controlled_buffer_2
  assign _1Y2 = not_1_out ? _1A2 : 1'bz;  // Controlled_Buffer controlled_buffer_3
  assign _1Y3 = not_1_out ? _1A3 : 1'bz;  // Controlled_Buffer controlled_buffer_4
  assign _2Y0 = not_2_out ? _2A0 : 1'bz;  // Controlled_Buffer controlled_buffer_5
  assign _2Y1 = not_2_out ? _2A1 : 1'bz;  // Controlled_Buffer controlled_buffer_6
  assign _2Y2 = not_2_out ? _2A2 : 1'bz;  // Controlled_Buffer controlled_buffer_7
  assign _2Y3 = not_2_out ? _2A3 : 1'bz;  // Controlled_Buffer controlled_buffer_8
  not not_2 (not_2_out, _2OE);

  assign GND = 1'b0;
  assign VCC = 1'b1;
endmodule

module _744017_DecadeCounter (
  input  MR,
  input  CP,
  input  nCE,
  output O5,
  output VCC,
  output O1,
  output O0,
  output O2,
  output O6,
  output TC,
  output O7,
  output O9,
  output O3,
  output O4,
  output GND,
  output O8
);

  wire and_1_out, and_2_out, decoder_1_out10, or_1_out, or_2_out;
  wire [3:0] counter_1_q;

  Counter #(.width(4), .max('hf)) counter_1 (
    .load(1'b0), .count(1'b1), .Q(counter_1_q), .clk(or_2_out), .clr(or_1_out));  // open: D, carry
  or or_1 (or_1_out, MR, decoder_1_out10);
  or or_2 (or_2_out, and_2_out, and_1_out);
  and and_1 (and_1_out, CP, ~nCE);  // AND_Gate
  Decoder #(.select(4)) decoder_1 (
    .out0(O0), .out1(O1), .out2(O2), .out3(O3), .out4(O4), .out5(O5), .out6(O6), .out7(O7), .out8(O8),
    .out9(O9), .out10(decoder_1_out10), .sel(counter_1_q), .en(1'b1));  // open: out11, out12, out13, out14, out15
  and and_2 (and_2_out, CP, ~MR, ~nCE);  // AND_Gate

  assign GND = 1'b0;
  assign VCC = 1'b1;
endmodule

module ALU (
  input  in_1,
  input  in_2,
  input  in_3,
  input  in_4,
  input  in_5,
  input  in_6,
  input  in_7,
  input  in_8,
  input  in_9,
  input  in_10,
  input  in_11,
  input  in_12,
  input  in_13,
  input  in_14,
  input  in_15,
  input  in_16,
  input  in_17,
  input  in_18,
  input  in_19,
  input  in_20,
  input  in_21,
  input  in_22,
  input  in_23,
  input  in_24,
  input  in_25,
  input  in_26,
  input  in_27,
  input  in_28,
  input  in_29,
  input  in_30,
  input  in_31,
  input  in_32,
  input  in_33,
  input  in_34
);

  wire n7404_hexinverter_1__1y, n7404_hexinverter_1__2y, n7404_hexinverter_1__3y, n7404_hexinverter_1__4y,
       n7404_hexinverter_1__5y, n7404_hexinverter_1__6y, n7404_hexinverter_2__1y, n7404_hexinverter_2__2y,
       n7404_hexinverter_2__3y, n7404_hexinverter_2__4y, n7404_hexinverter_2__5y, n7404_hexinverter_2__6y,
       n7404_hexinverter_3__1y, n7404_hexinverter_3__2y, n7404_hexinverter_3__3y, n7404_hexinverter_3__5y,
       n7404_hexinverter_3__6y, n74283_4bitadder_1_c4, n74283_4bitadder_1_sum1, n74283_4bitadder_1_sum2,
       n74283_4bitadder_1_sum3, n74283_4bitadder_1_sum4, n74283_4bitadder_2_c4, n74283_4bitadder_2_sum1,
       n74283_4bitadder_2_sum2, n74283_4bitadder_2_sum3, n74283_4bitadder_2_sum4, n74283_4bitadder_3_c4,
       n74283_4bitadder_3_sum1, n74283_4bitadder_3_sum2, n74283_4bitadder_3_sum3, n74283_4bitadder_3_sum4,
       n74283_4bitadder_4_sum1, n74283_4bitadder_4_sum2, n74283_4bitadder_4_sum3, n74283_4bitadder_4_sum4,
       n74374_octalreg_1_q1, n74374_octalreg_1_q2, n74374_octalreg_1_q3, n74374_octalreg_1_q4,
       n74374_octalreg_1_q5, n74374_octalreg_1_q6, n74374_octalreg_1_q7, n74374_octalreg_1_q8,
       n74374_octalreg_2_q1, n74374_octalreg_2_q2, n74374_octalreg_2_q3, n74374_octalreg_2_q4,
       n74374_octalreg_2_q5, n74374_octalreg_2_q6, n74374_octalreg_2_q7, n74374_octalreg_2_q8,
       n74374_octalreg_3_q1, n74374_octalreg_3_q2, n74374_octalreg_3_q3, n74374_octalreg_3_q4,
       n74374_octalreg_3_q5, n74374_octalreg_3_q6, n74374_octalreg_3_q7, n74374_octalreg_3_q8,
       n74374_octalreg_4_q1, n74374_octalreg_4_q2, n74374_octalreg_4_q3, n74374_octalreg_4_q4,
       n74374_octalreg_4_q5, n74374_octalreg_4_q6, n74374_octalreg_4_q7, n74374_octalreg_4_q8, undriven;

  _74244_OctalTriStateBuffer u_74244_octaltristatebuffer_1 ();  // open: _1OE, _1A0, _2Y0, _1A1, _2Y1, _1A2, _2Y2, _1A3, _2Y3, GND, VCC, _2OE, _1Y0, _2A0, _1Y1, _2A1, _1Y2, _2A2, _1Y3, _2A3
  _74244_OctalTriStateBuffer u_74244_octaltristatebuffer_2 ();  // open: _1OE, _1A0, _2Y0, _1A1, _2Y1, _1A2, _2Y2, _1A3, _2Y3, GND, VCC, _2OE, _1Y0, _2A0, _1Y1, _2A1, _1Y2, _2A2, _1Y3, _2A3
  _744075_triple3InputOR u_744075_triple3inputor_1 ();  // open: _2A, _2B, _1A, _1B, _1C, _1Y, GND, VCC, _3C, _3B, _3A, _3Y, _2Y, _2C
  _744075_triple3InputOR u_744075_triple3inputor_2 ();  // open: _2A, _2B, _1A, _1B, _1C, _1Y, GND, VCC, _3C, _3B, _3A, _3Y, _2Y, _2C
  _744075_triple3InputOR u_744075_triple3inputor_3 ();  // open: _2A, _2B, _1A, _1B, _1C, _1Y, GND, VCC, _3C, _3B, _3A, _3Y, _2Y, _2C
  _74283_4bitAdder u_74283_4bitadder_1 (
    .Sum2(n74283_4bitadder_1_sum2), .B2(n74374_octalreg_1_q2), .A2(n7404_hexinverter_1__2y),
    .Sum1(n74283_4bitadder_1_sum1), .A1(n7404_hexinverter_1__1y), .B1(n74374_octalreg_1_q1), .C0(1'b1),
    .B3(n74374_octalreg_1_q3), .A3(n7404_hexinverter_1__6y), .Sum3(n74283_4bitadder_1_sum3),
    .A4(n7404_hexinverter_1__5y), .B4(n74374_octalreg_1_q4), .Sum4(n74283_4bitadder_1_sum4),
    .C4(n74283_4bitadder_1_c4));  // open: GND, Vcc
  _74283_4bitAdder u_74283_4bitadder_2 (
    .Sum2(n74283_4bitadder_2_sum2), .B2(n74374_octalreg_1_q6), .A2(n7404_hexinverter_1__3y),
    .Sum1(n74283_4bitadder_2_sum1), .A1(n7404_hexinverter_1__4y), .B1(n74374_octalreg_1_q5),
    .C0(n74283_4bitadder_1_c4), .B3(n74374_octalreg_1_q7), .A3(n7404_hexinverter_2__1y),
    .Sum3(n74283_4bitadder_2_sum3), .A4(n7404_hexinverter_2__2y), .B4(n74374_octalreg_1_q8),
    .Sum4(n74283_4bitadder_2_sum4), .C4(n74283_4bitadder_2_c4));  // open: GND, Vcc
  _74283_4bitAdder u_74283_4bitadder_3 (
    .Sum2(n74283_4bitadder_3_sum2), .B2(n74374_octalreg_2_q2), .A2(n7404_hexinverter_2__5y),
    .Sum1(n74283_4bitadder_3_sum1), .A1(n7404_hexinverter_2__6y), .B1(n74374_octalreg_2_q1),
    .C0(n74283_4bitadder_2_c4), .B3(n74374_octalreg_2_q3), .A3(n7404_hexinverter_2__4y),
    .Sum3(n74283_4bitadder_3_sum3), .A4(n7404_hexinverter_2__3y), .B4(n74374_octalreg_2_q4),
    .Sum4(n74283_4bitadder_3_sum4), .C4(n74283_4bitadder_3_c4));  // open: GND, Vcc
  _74283_4bitAdder u_74283_4bitadder_4 (
    .Sum2(n74283_4bitadder_4_sum2), .B2(n74374_octalreg_2_q6), .A2(n7404_hexinverter_3__2y),
    .Sum1(n74283_4bitadder_4_sum1), .A1(n7404_hexinverter_3__1y), .B1(n74374_octalreg_2_q5),
    .C0(n74283_4bitadder_3_c4), .B3(n74374_octalreg_2_q7), .A3(n7404_hexinverter_3__6y),
    .Sum3(n74283_4bitadder_4_sum3), .A4(n7404_hexinverter_3__5y), .B4(n74374_octalreg_2_q8),
    .Sum4(n74283_4bitadder_4_sum4));  // open: GND, Vcc, C4
  _7404_HexInverter u_7404_hexinverter_1 (
    ._1A(n74374_octalreg_3_q2), ._1Y(n7404_hexinverter_1__1y), ._2A(n74374_octalreg_3_q1),
    ._2Y(n7404_hexinverter_1__2y), ._3A(n74374_octalreg_3_q6), ._3Y(n7404_hexinverter_1__3y),
    ._6A(n74374_octalreg_3_q3), ._6Y(n7404_hexinverter_1__6y), ._5A(n74374_octalreg_3_q4),
    ._5Y(n7404_hexinverter_1__5y), ._4A(n74374_octalreg_3_q5), ._4Y(n7404_hexinverter_1__4y));  // open: GND, VCC
  _7404_HexInverter u_7404_hexinverter_2 (
    ._1A(n74374_octalreg_3_q8), ._1Y(n7404_hexinverter_2__1y), ._2A(n74374_octalreg_3_q7),
    ._2Y(n7404_hexinverter_2__2y), ._3A(n74374_octalreg_4_q4), ._3Y(n7404_hexinverter_2__3y),
    ._6A(n74374_octalreg_4_q1), ._6Y(n7404_hexinverter_2__6y), ._5A(n74374_octalreg_4_q2),
    ._5Y(n7404_hexinverter_2__5y), ._4A(n74374_octalreg_4_q3), ._4Y(n7404_hexinverter_2__4y));  // open: GND, VCC
  _7404_HexInverter u_7404_hexinverter_3 (
    ._1A(n74374_octalreg_4_q6), ._1Y(n7404_hexinverter_3__1y), ._2A(n74374_octalreg_4_q5),
    ._2Y(n7404_hexinverter_3__2y), ._3A(undriven), ._3Y(n7404_hexinverter_3__3y), ._6A(n74374_octalreg_4_q7),
    ._6Y(n7404_hexinverter_3__6y), ._5A(n74374_octalreg_4_q8), ._5Y(n7404_hexinverter_3__5y));  // open: GND, VCC, _4A, _4Y
  _74374_OctalReg u_74374_octalreg_1 (
    .OUTPUT_CONTROL(1'b1), .Q1(n74374_octalreg_1_q1), .D1(in_2), .D2(in_3), .Q2(n74374_octalreg_1_q2),
    .Q3(n74374_octalreg_1_q3), .D3(in_5), .D4(in_4), .Q4(n74374_octalreg_1_q4), .Q8(n74374_octalreg_1_q8),
    .D8(in_9), .D7(in_8), .Q7(n74374_octalreg_1_q7), .Q6(n74374_octalreg_1_q6), .D6(in_7), .D5(in_6),
    .Q5(n74374_octalreg_1_q5), .CLOCK(in_1));  // open: GND, VCC
  _74374_OctalReg u_74374_octalreg_2 (
    .OUTPUT_CONTROL(1'b1), .Q1(n74374_octalreg_2_q1), .D1(in_10), .D2(in_11), .Q2(n74374_octalreg_2_q2),
    .Q3(n74374_octalreg_2_q3), .D3(in_13), .D4(in_12), .Q4(n74374_octalreg_2_q4), .Q8(n74374_octalreg_2_q8),
    .D8(in_17), .D7(in_16), .Q7(n74374_octalreg_2_q7), .Q6(n74374_octalreg_2_q6), .D6(in_15), .D5(in_14),
    .Q5(n74374_octalreg_2_q5), .CLOCK(in_1));  // open: GND, VCC
  _74374_OctalReg u_74374_octalreg_3 (
    .OUTPUT_CONTROL(1'b1), .Q1(n74374_octalreg_3_q1), .D1(in_19), .D2(in_20), .Q2(n74374_octalreg_3_q2),
    .Q3(n74374_octalreg_3_q3), .D3(in_22), .D4(in_21), .Q4(n74374_octalreg_3_q4), .Q8(n74374_octalreg_3_q8),
    .D8(in_26), .D7(in_25), .Q7(n74374_octalreg_3_q7), .Q6(n74374_octalreg_3_q6), .D6(in_24), .D5(in_23),
    .Q5(n74374_octalreg_3_q5), .CLOCK(in_18));  // open: GND, VCC
  _74374_OctalReg u_74374_octalreg_4 (
    .OUTPUT_CONTROL(1'b1), .Q1(n74374_octalreg_4_q1), .D1(in_27), .D2(in_28), .Q2(n74374_octalreg_4_q2),
    .Q3(n74374_octalreg_4_q3), .D3(in_30), .D4(in_29), .Q4(n74374_octalreg_4_q4), .Q8(n74374_octalreg_4_q8),
    .D8(in_34), .D7(in_33), .Q7(n74374_octalreg_4_q7), .Q6(n74374_octalreg_4_q6), .D6(in_32), .D5(in_31),
    .Q5(n74374_octalreg_4_q5), .CLOCK(in_18));  // open: GND, VCC
endmodule

module _7408_QuadAND (
  input  _1A,
  input  _1B,
  input  _4B,
  input  _4A,
  input  _2A,
  input  _2B,
  input  _3B,
  input  _3A,
  output VCC,
  output _1Y,
  output _4Y,
  output _2Y,
  output GND,
  output _3Y
);

  and and_1 (_1Y, _1B, _1A);
  and and_2 (_2Y, _2B, _2A);
  and and_3 (_4Y, _4A, _4B);
  and and_4 (_3Y, _3A, _3B);

  assign GND = 1'b0;
  assign VCC = 1'b1;
endmodule

module _7404_HexInverter (
  input  _1A,
  input  _6A,
  input  _2A,
  input  _5A,
  input  _3A,
  input  _4A,
  output VCC,
  output _1Y,
  output _6Y,
  output _2Y,
  output _5Y,
  output _3Y,
  output GND,
  output _4Y
);

  not not_1 (_1Y, _1A);
  not not_2 (_2Y, _2A);
  not not_3 (_3Y, _3A);
  not not_4 (_6Y, _6A);
  not not_5 (_5Y, _5A);
  not not_6 (_4Y, _4A);

  assign GND = 1'b0;
  assign VCC = 1'b1;
endmodule

module _7400_QuadNAND (
  input  _1A,
  input  _1B,
  input  _4B,
  input  _4A,
  input  _2A,
  input  _2B,
  input  _3B,
  input  _3A,
  output VCC,
  output _1Y,
  output _4Y,
  output _2Y,
  output GND,
  output _3Y
);

  nand nand_1 (_1Y, _1B, _1A);
  nand nand_2 (_2Y, _2B, _2A);
  nand nand_3 (_4Y, _4A, _4B);
  nand nand_4 (_3Y, _3A, _3B);

  assign GND = 1'b0;
  assign VCC = 1'b1;
endmodule

module DesignIdea2 (
  input  in_1
);

  wire and_1_out, and_2_out, and_3_out, and_4_out, and_5_out, clock_1_out, decoder_1_out0, decoder_1_out1,
       decoder_1_out2, decoder_1_out3, decoder_2_out0, decoder_2_out1, decoder_2_out2, decoder_2_out3,
       decoder_2_out4, decoder_2_out5, decoder_2_out6, decoder_2_out7, nor_1_out, not_1_out, not_3_out,
       not_4_out, not_5_out, not_6_out, not_7_out, not_8_out, or_1_out, or_2_out, or_3_out, or_4_out,
       or_5_out, or_6_out;
  wire [1:0] controlled_buffer_2_out;
  wire [2:0] counter_2_q;
  wire [15:0] adder_1_out, controlled_buffer_1_out, counter_1_q, not_2_out, register_1_q, register_2_q,
       register_3_q;
  wire [15:2] controlled_buffer_2_out_2;

  Clock clock_1 (.out(clock_1_out));
  not not_1 (not_1_out, clock_1_out);
  Register #(.width(16)) register_1 (
    .D(controlled_buffer_1_out), .en(or_3_out), .Q(register_1_q), .clk(clock_1_out), .clr(in_1));
  Counter #(.width(16), .max('hffff)) counter_1 (
    .load(and_4_out), .D({controlled_buffer_2_out_2, controlled_buffer_2_out}), .count(or_4_out),
    .Q(counter_1_q), .clk(clock_1_out), .clr(in_1));  // open: carry
  Register #(.width(16)) register_2 (
    .D(controlled_buffer_1_out), .en(decoder_2_out1), .Q(register_2_q), .clk(clock_1_out), .clr(in_1));
  assign not_2_out = ~register_3_q;  // NOT_Gate not_2, 16 bits wide
  Register #(.width(16)) register_3 (
    .D(controlled_buffer_1_out), .en(decoder_2_out3), .Q(register_3_q), .clk(clock_1_out), .clr(in_1));
  assign controlled_buffer_1_out = decoder_2_out4 ? adder_1_out : 16'bz;  // Controlled_Buffer controlled_buffer_1
  assign {controlled_buffer_2_out_2, controlled_buffer_2_out} = or_2_out ? register_1_q : 16'bz;  // Controlled_Buffer controlled_buffer_2
  assign {controlled_buffer_2_out_2, controlled_buffer_2_out} = or_3_out ? counter_1_q : 16'bz;  // Controlled_Buffer controlled_buffer_3
  Decoder #(.select(2)) decoder_1 (
    .out0(decoder_1_out0), .out1(decoder_1_out1), .out2(decoder_1_out2), .out3(decoder_1_out3),
    .sel(controlled_buffer_2_out), .en(1'b1));
  Adder #(.width(16)) adder_1 (.a(register_2_q), .b(not_2_out), .out(adder_1_out), .cin(1'b1));  // open: cout
  and and_1 (and_1_out, controlled_buffer_2_out_2[2], controlled_buffer_2_out_2[3], controlled_buffer_2_out_2[4], controlled_buffer_2_out_2[5], controlled_buffer_2_out_2[6], controlled_buffer_2_out_2[7], controlled_buffer_2_out_2[8], controlled_buffer_2_out_2[9], controlled_buffer_2_out_2[10], controlled_buffer_2_out_2[11], controlled_buffer_2_out_2[12], controlled_buffer_2_out_2[13], controlled_buffer_2_out_2[14], controlled_buffer_2_out_2[15]);
  not not_3 (not_3_out, and_1_out);
  not not_4 (not_4_out, controlled_buffer_2_out_2[15]);
  nor nor_1 (nor_1_out, adder_1_out[0], adder_1_out[1], adder_1_out[2], adder_1_out[3], adder_1_out[4], adder_1_out[5], adder_1_out[6], adder_1_out[7], adder_1_out[9], adder_1_out[10], adder_1_out[11], adder_1_out[12], adder_1_out[13], adder_1_out[14], adder_1_out[15], adder_1_out[8]);
  and and_2 (and_2_out, not_3_out, controlled_buffer_2_out_2[15]);
  or or_1 (or_1_out, nor_1_out, adder_1_out[15]);
  not not_5 (not_5_out, not_4_out);
  or or_2 (or_2_out, decoder_2_out1, decoder_2_out3, decoder_2_out4, and_4_out);
  or or_3 (or_3_out, decoder_2_out0, decoder_2_out2, decoder_2_out5);
  or or_4 (or_4_out, decoder_2_out1, decoder_2_out3, and_5_out);
  and and_3 (and_3_out, decoder_2_out4, not_1_out);
  not not_6 (not_6_out, and_3_out);
  not not_7 (not_7_out, and_2_out);
  and and_4 (and_4_out, or_1_out, decoder_2_out6);
  and and_5 (and_5_out, ~or_1_out, decoder_2_out6);  // AND_Gate
  or or_5 (or_5_out, decoder_2_out0, decoder_2_out1, decoder_2_out2, decoder_2_out3, decoder_2_out5);
  not not_8 (not_8_out, or_5_out);
  Counter #(.width(3), .max('h7)) counter_2 (
    .load(1'b0), .count(1'b1), .Q(counter_2_q), .clk(not_1_out), .clr(or_6_out));  // open: D, carry
  Decoder #(.select(3)) decoder_2 (
    .out0(decoder_2_out0), .out1(decoder_2_out1), .out2(decoder_2_out2), .out3(decoder_2_out3),
    .out4(decoder_2_out4), .out5(decoder_2_out5), .out6(decoder_2_out6), .out7(decoder_2_out7),
    .sel(counter_2_q), .en(1'b1));
  or or_6 (or_6_out, in_1, decoder_2_out7);

  // Notes on the sheet:
  //   adrIoSelect
  //   adrRamSelect
  //   adrRomSelect
  //   /CErom
  //   /CLK
  //   /WEram
  //   /CEram
  //   Write Mem
  //   Read Mem
  //   /OEram
endmodule

module _7432_QuadOR (
  input  _1A,
  input  _1B,
  input  _4B,
  input  _4A,
  input  _2A,
  input  _2B,
  input  _3B,
  input  _3A,
  output VCC,
  output _1Y,
  output _4Y,
  output _2Y,
  output GND,
  output _3Y
);

  or or_1 (_1Y, _1B, _1A);
  or or_2 (_2Y, _2B, _2A);
  or or_3 (_4Y, _4A, _4B);
  or or_4 (_3Y, _3A, _3B);

  assign GND = 1'b0;
  assign VCC = 1'b1;
endmodule

module _744075_triple3InputOR (
  input  _2A,
  input  _2B,
  input  _3C,
  input  _1A,
  input  _3B,
  input  _1B,
  input  _3A,
  input  _1C,
  input  _2C,
  output VCC,
  output _3Y,
  output _1Y,
  output _2Y,
  output GND
);

  or or_1 (_1Y, _1C, _1B, _1A);
  or or_2 (_3Y, _3C, _3B, _3A);
  or or_3 (_2Y, _2A, _2B, _2C);

  assign GND = 1'b0;
  assign VCC = 1'b1;
endmodule

module _7411_triple3InputAND (
  input  _1A,
  input  _1B,
  input  _1C,
  input  _2A,
  input  _2B,
  input  _3C,
  input  _2C,
  input  _3B,
  input  _3A,
  output VCC,
  output _1Y,
  output _2Y,
  output GND,
  output _3Y
);

  and and_1 (_2Y, _2C, _2B, _2A);
  and and_2 (_1Y, _1B, _1A, _1C);
  and and_3 (_3Y, _3C, _3B, _3A);

  assign GND = 1'b0;
  assign VCC = 1'b1;
endmodule

module _4516_4BitCounterPresettable (
  input  PRESET_ENABLE,
  input  CLOCK,
  input  P4,
  input  P1,
  input  P3,
  input  nCARRYIN,
  input  P2,
  input  UP_DOWN,
  input  RESET,
  output VDD,
  output Q4,
  output Q3,
  output Q1,
  output Q2,
  output nCARRYOUT,
  output VSS
);

  wire counter_1_carry, nor_1_out, nor_2_out, or_1_out, or_2_out;

  not not_1 (nCARRYOUT, counter_1_carry);
  or or_1 (or_1_out, PRESET_ENABLE, nor_1_out);
  nor nor_1 (nor_1_out, UP_DOWN, nCARRYIN);
  nor nor_2 (nor_2_out, PRESET_ENABLE, nCARRYIN);
  Counter #(.width(4), .max('hf)) counter_1 (
    .load(or_1_out), .D({P4, P3, P2, P1}), .count(nor_2_out), .Q({Q4, Q3, Q2, Q1}), .carry(counter_1_carry),
    .clk(or_2_out), .clr(RESET));
  or or_2 (or_2_out, PRESET_ENABLE, CLOCK);

  assign VDD = 1'b1;
  assign VSS = 1'b0;
endmodule
